// Logisim project ProcessorNamık.circ as structural Verilog: 19 circuits, main circuit SR Latch
module SR_Latch (
  input  S__set,
  input  R__reset,
  output Q
);

  wire nor_1_out;

  nor nor_1 (nor_1_out, S__set, Q);
  nor nor_2 (Q, nor_1_out, R__reset);
endmodule

module D_Latch (
  input  D,
  input  clk,
  output Q
);

  wire and_1_out, and_2_out, not_1_out;

  not not_1 (not_1_out, D);
  and and_1 (and_1_out, D, clk);
  and and_2 (and_2_out, clk, not_1_out);
  SR_Latch SR_Latch (.S__set(and_1_out), .R__reset(and_2_out), .Q(Q));
endmodule

module D_Flip_Flop (
  input  D,
  input  clk,
  output Q
);

  wire D_Latch__master_q, not_1_out;

  not not_1 (not_1_out, clk);
  D_Latch D_Latch__master (.D(D), .clk(not_1_out), .Q(D_Latch__master_q));
  D_Latch D_Latch__servant (.D(D_Latch__master_q), .clk(clk), .Q(Q));
endmodule

// 2 R
module _2_bit_Register (
  input  I1,
  input  I0,
  input  clk,
  output Q1,
  output Q0
);

  D_Flip_Flop Flip_Flop (.D(I1), .clk(clk), .Q(Q1));
  D_Flip_Flop Flip_Flop_2 (.D(I0), .clk(clk), .Q(Q0));
endmodule

// 4 R
module _4_bit_Register (
  input  I3,
  input  I2,
  input  I1,
  input  I0,
  input  clk,
  output Q3,
  output Q2,
  output Q1,
  output Q0
);

  _2_bit_Register u_2_bit_register_1 (.clk(clk), .I1(I3), .I0(I2), .Q1(Q3), .Q0(Q2));
  _2_bit_Register u_2_bit_register_2 (.clk(clk), .I1(I1), .I0(I0), .Q1(Q1), .Q0(Q0));
endmodule

// 8 R
module _8_bit_Register (
  input  I7,
  input  I6,
  input  I5,
  input  I4,
  input  I3,
  input  I2,
  input  I1,
  input  I0,
  input  clk,
  output Q7,
  output Q6,
  output Q5,
  output Q4,
  output Q3,
  output Q2,
  output Q1,
  output Q0
);

  _4_bit_Register u_4_bit_register_1 (
    .clk(clk), .I3(I7), .I2(I6), .I1(I5), .I0(I4), .Q3(Q7), .Q2(Q6), .Q1(Q5), .Q0(Q4));
  _4_bit_Register u_4_bit_register_2 (
    .clk(clk), .I3(I3), .I2(I2), .I1(I1), .I0(I0), .Q3(Q3), .Q2(Q2), .Q1(Q1), .Q0(Q0));
endmodule

module _12_bit_Register (
  input  I11,
  input  I10,
  input  I9,
  input  I8,
  input  I7,
  input  I6,
  input  I5,
  input  I4,
  input  I3,
  input  I2,
  input  I1,
  input  I0,
  input  clk,
  output Q11,
  output Q10,
  output Q9,
  output Q8,
  output Q7,
  output Q6,
  output Q5,
  output Q4,
  output Q3,
  output Q2,
  output Q1,
  output Q0
);

  _8_bit_Register u_8_bit_register_1 (
    .clk(clk), .I7(I11), .I6(I10), .I5(I9), .I4(I8), .I3(I7), .I2(I6), .I1(I5), .I0(I4), .Q7(Q11), .Q6(Q10),
    .Q5(Q9), .Q4(Q8), .Q3(Q7), .Q2(Q6), .Q1(Q5), .Q0(Q4));
  _4_bit_Register u_4_bit_register_1 (
    .clk(clk), .I3(I3), .I2(I2), .I1(I1), .I0(I0), .Q3(Q3), .Q2(Q2), .Q1(Q1), .Q0(Q0));
endmodule

module _16_bit_Register (
  input  I15,
  input  I14,
  input  I13,
  input  I12,
  input  I11,
  input  I10,
  input  I9,
  input  I8,
  input  I7,
  input  I6,
  input  I5,
  input  I4,
  input  I3,
  input  I2,
  input  I1,
  input  I0,
  input  clk,
  output Q15,
  output Q14,
  output Q13,
  output Q12,
  output Q11,
  output Q10,
  output Q9,
  output Q8,
  output Q7,
  output Q6,
  output Q5,
  output Q4,
  output Q3,
  output Q2,
  output Q1,
  output Q0
);

  _8_bit_Register u_8_bit_register_1 (
    .clk(clk), .I7(I15), .I6(I14), .I5(I13), .I4(I12), .I3(I11), .I2(I10), .I1(I9), .I0(I8), .Q7(Q15),
    .Q6(Q14), .Q5(Q13), .Q4(Q12), .Q3(Q11), .Q2(Q10), .Q1(Q9), .Q0(Q8));
  _8_bit_Register u_8_bit_register_2 (
    .clk(clk), .I7(I7), .I6(I6), .I5(I5), .I4(I4), .I3(I3), .I2(I2), .I1(I1), .I0(I0), .Q7(Q7), .Q6(Q6),
    .Q5(Q5), .Q4(Q4), .Q3(Q3), .Q2(Q2), .Q1(Q1), .Q0(Q0));
endmodule

// Reg-File
module Register_File (
  input  [3:0] read_register1,
  input  [3:0] read_register2,
  input  [3:0] write_register,
  input  [15:0] value,
  input  write,
  input  clk,
  output [15:0] output1,
  output [15:0] output2
);

  wire decoder_1_out0, decoder_1_out1, decoder_1_out2, decoder_1_out3, decoder_1_out4, decoder_1_out5,
       decoder_1_out6, decoder_1_out7, decoder_1_out8, decoder_1_out9, decoder_1_out10, decoder_1_out11,
       decoder_1_out12, decoder_1_out13, decoder_1_out14, decoder_1_out15, decoder_2_out0, decoder_2_out1,
       decoder_2_out2, decoder_2_out3, decoder_2_out4, decoder_2_out5, decoder_2_out6, decoder_2_out7,
       decoder_2_out8, decoder_2_out9, decoder_2_out10, decoder_2_out11, decoder_2_out12, decoder_2_out13,
       decoder_2_out14, decoder_2_out15, decoder_3_out0, decoder_3_out1, decoder_3_out2, decoder_3_out3,
       decoder_3_out4, decoder_3_out5, decoder_3_out6, decoder_3_out7, decoder_3_out8, decoder_3_out9,
       decoder_3_out10, decoder_3_out11, decoder_3_out12, decoder_3_out13, decoder_3_out14, decoder_3_out15,
       not_1_out;
  wire [15:0] register_1_q, register_2_q, register_3_q, register_4_q, register_5_q, register_6_q,
       register_7_q, register_8_q, register_9_q, register_10_q, register_11_q, register_12_q, register_13_q,
       register_14_q, register_15_q, register_16_q;

  Decoder #(.select(4), .disabled(0)) decoder_1 (
    .out0(decoder_1_out0), .out1(decoder_1_out1), .out2(decoder_1_out2), .out3(decoder_1_out3),
    .out4(decoder_1_out4), .out5(decoder_1_out5), .out6(decoder_1_out6), .out7(decoder_1_out7),
    .out8(decoder_1_out8), .out9(decoder_1_out9), .out10(decoder_1_out10), .out11(decoder_1_out11),
    .out12(decoder_1_out12), .out13(decoder_1_out13), .out14(decoder_1_out14), .out15(decoder_1_out15),
    .sel(read_register1), .en(not_1_out));
  Decoder #(.select(4), .disabled(0)) decoder_2 (
    .out0(decoder_2_out0), .out1(decoder_2_out1), .out2(decoder_2_out2), .out3(decoder_2_out3),
    .out4(decoder_2_out4), .out5(decoder_2_out5), .out6(decoder_2_out6), .out7(decoder_2_out7),
    .out8(decoder_2_out8), .out9(decoder_2_out9), .out10(decoder_2_out10), .out11(decoder_2_out11),
    .out12(decoder_2_out12), .out13(decoder_2_out13), .out14(decoder_2_out14), .out15(decoder_2_out15),
    .sel(read_register2), .en(not_1_out));
  not not_1 (not_1_out, write);
  Decoder #(.select(4), .disabled(0)) decoder_3 (
    .out0(decoder_3_out0), .out1(decoder_3_out1), .out2(decoder_3_out2), .out3(decoder_3_out3),
    .out4(decoder_3_out4), .out5(decoder_3_out5), .out6(decoder_3_out6), .out7(decoder_3_out7),
    .out8(decoder_3_out8), .out9(decoder_3_out9), .out10(decoder_3_out10), .out11(decoder_3_out11),
    .out12(decoder_3_out12), .out13(decoder_3_out13), .out14(decoder_3_out14), .out15(decoder_3_out15),
    .sel(write_register), .en(write));
  Register #(.width(16)) register_1 (.D(value), .en(decoder_3_out0), .Q(register_1_q), .clk(clk));  // open: clr
  Register #(.width(16)) register_2 (.D(value), .en(decoder_3_out1), .Q(register_2_q), .clk(clk));  // open: clr
  Register #(.width(16)) register_3 (.D(value), .en(decoder_3_out2), .Q(register_3_q), .clk(clk));  // open: clr
  Register #(.width(16)) register_4 (.D(value), .en(decoder_3_out3), .Q(register_4_q), .clk(clk));  // open: clr
  Register #(.width(16)) register_5 (.D(value), .en(decoder_3_out4), .Q(register_5_q), .clk(clk));  // open: clr
  Register #(.width(16)) register_6 (.D(value), .en(decoder_3_out5), .Q(register_6_q), .clk(clk));  // open: clr
  Register #(.width(16)) register_7 (.D(value), .en(decoder_3_out6), .Q(register_7_q), .clk(clk));  // open: clr
  Register #(.width(16)) register_8 (.D(value), .en(decoder_3_out7), .Q(register_8_q), .clk(clk));  // open: clr
  assign output1 = decoder_1_out0 ? register_1_q : 16'bz;  // Controlled_Buffer controlled_buffer_1
  assign output2 = decoder_2_out0 ? register_1_q : 16'bz;  // Controlled_Buffer controlled_buffer_2
  assign output1 = decoder_1_out1 ? register_2_q : 16'bz;  // Controlled_Buffer controlled_buffer_3
  assign output2 = decoder_2_out1 ? register_2_q : 16'bz;  // Controlled_Buffer controlled_buffer_4
  assign output1 = decoder_1_out2 ? register_3_q : 16'bz;  // Controlled_Buffer controlled_buffer_5
  assign output2 = decoder_2_out2 ? register_3_q : 16'bz;  // Controlled_Buffer controlled_buffer_6
  assign output1 = decoder_1_out3 ? register_4_q : 16'bz;  // Controlled_Buffer controlled_buffer_7
  assign output2 = decoder_2_out3 ? register_4_q : 16'bz;  // Controlled_Buffer controlled_buffer_8
  assign output1 = decoder_1_out4 ? register_5_q : 16'bz;  // Controlled_Buffer controlled_buffer_9
  assign output2 = decoder_2_out4 ? register_5_q : 16'bz;  // Controlled_Buffer controlled_buffer_10
  assign output1 = decoder_1_out5 ? register_6_q : 16'bz;  // Controlled_Buffer controlled_buffer_11
  assign output2 = decoder_2_out5 ? register_6_q : 16'bz;  // Controlled_Buffer controlled_buffer_12
  assign output1 = decoder_1_out6 ? register_7_q : 16'bz;  // Controlled_Buffer controlled_buffer_13
  assign output2 = decoder_2_out6 ? register_7_q : 16'bz;  // Controlled_Buffer controlled_buffer_14
  assign output1 = decoder_1_out7 ? register_8_q : 16'bz;  // Controlled_Buffer controlled_buffer_15
  assign output2 = decoder_2_out7 ? register_8_q : 16'bz;  // Controlled_Buffer controlled_buffer_16
  Register #(.width(16)) register_9 (.D(value), .en(decoder_3_out8), .Q(register_9_q), .clk(clk));  // open: clr
  Register #(.width(16)) register_10 (.D(value), .en(decoder_3_out9), .Q(register_10_q), .clk(clk));  // open: clr
  Register #(.width(16)) register_11 (.D(value), .en(decoder_3_out10), .Q(register_11_q), .clk(clk));  // open: clr
  Register #(.width(16)) register_12 (.D(value), .en(decoder_3_out11), .Q(register_12_q), .clk(clk));  // open: clr
  Register #(.width(16)) register_13 (.D(value), .en(decoder_3_out12), .Q(register_13_q), .clk(clk));  // open: clr
  Register #(.width(16)) register_14 (.D(value), .en(decoder_3_out13), .Q(register_14_q), .clk(clk));  // open: clr
  Register #(.width(16)) register_15 (.D(value), .en(decoder_3_out14), .Q(register_15_q), .clk(clk));  // open: clr
  Register #(.width(16)) register_16 (.D(value), .en(decoder_3_out15), .Q(register_16_q), .clk(clk));  // open: clr
  assign output1 = decoder_1_out8 ? register_9_q : 16'bz;  // Controlled_Buffer controlled_buffer_17
  assign output2 = decoder_2_out8 ? register_9_q : 16'bz;  // Controlled_Buffer controlled_buffer_18
  assign output1 = decoder_1_out9 ? register_10_q : 16'bz;  // Controlled_Buffer controlled_buffer_19
  assign output2 = decoder_2_out9 ? register_10_q : 16'bz;  // Controlled_Buffer controlled_buffer_20
  assign output1 = decoder_1_out10 ? register_11_q : 16'bz;  // Controlled_Buffer controlled_buffer_21
  assign output2 = decoder_2_out10 ? register_11_q : 16'bz;  // Controlled_Buffer controlled_buffer_22
  assign output1 = decoder_1_out11 ? register_12_q : 16'bz;  // Controlled_Buffer controlled_buffer_23
  assign output2 = decoder_2_out11 ? register_12_q : 16'bz;  // Controlled_Buffer controlled_buffer_24
  assign output1 = decoder_1_out12 ? register_13_q : 16'bz;  // Controlled_Buffer controlled_buffer_25
  assign output2 = decoder_2_out12 ? register_13_q : 16'bz;  // Controlled_Buffer controlled_buffer_26
  assign output1 = decoder_1_out13 ? register_14_q : 16'bz;  // Controlled_Buffer controlled_buffer_27
  assign output2 = decoder_2_out13 ? register_14_q : 16'bz;  // Controlled_Buffer controlled_buffer_28
  assign output1 = decoder_1_out14 ? register_15_q : 16'bz;  // Controlled_Buffer controlled_buffer_29
  assign output2 = decoder_2_out14 ? register_15_q : 16'bz;  // Controlled_Buffer controlled_buffer_30
  assign output1 = decoder_1_out15 ? register_16_q : 16'bz;  // Controlled_Buffer controlled_buffer_31
  assign output2 = decoder_2_out15 ? register_16_q : 16'bz;  // Controlled_Buffer controlled_buffer_32
endmodule

// HA
module Half_Adder (
  input  a,
  input  b,
  output carry_out,
  output sum
);

  and and_1 (carry_out, b, a);
  xor xor_1 (sum, b, a);
endmodule

// FA
module Full_Adder (
  input  a,
  input  b,
  input  carry_in,
  output carry_out,
  output sum
);

  wire half_adder_1_carry_out, half_adder_1_sum, half_adder_2_carry_out;

  Half_Adder half_adder_1 (.a(a), .b(b), .carry_out(half_adder_1_carry_out), .sum(half_adder_1_sum));
  Half_Adder half_adder_2 (.a(half_adder_1_sum), .b(carry_in), .carry_out(half_adder_2_carry_out), .sum(sum));
  or or_1 (carry_out, half_adder_1_carry_out, half_adder_2_carry_out);
endmodule

// 4 A
module _4_bit_Adder (
  input  [3:0] a,
  input  [3:0] b,
  input  carry_in,
  output carry_out,
  output [3:0] \output 
);

  wire full_adder_1_carry_out, full_adder_2_carry_out, full_adder_3_carry_out;

  Full_Adder full_adder_1 (
    .a(a[0]), .b(b[0]), .carry_in(carry_in), .carry_out(full_adder_1_carry_out), .sum(\output [0]));
  Full_Adder full_adder_2 (
    .a(a[1]), .b(b[1]), .carry_in(full_adder_1_carry_out), .carry_out(full_adder_2_carry_out),
    .sum(\output [1]));
  Full_Adder full_adder_3 (
    .a(a[2]), .b(b[2]), .carry_in(full_adder_2_carry_out), .carry_out(full_adder_3_carry_out),
    .sum(\output [2]));
  Full_Adder full_adder_4 (
    .a(a[3]), .b(b[3]), .carry_in(full_adder_3_carry_out), .carry_out(carry_out), .sum(\output [3]));
endmodule

// 8 A
module _8_bit_Adder (
  input  [7:0] a,
  input  [7:0] b,
  input  carry_in,
  output carry_out,
  output [7:0] out_5
);

  wire n4_bit_adder_1_carry_out;

  _4_bit_Adder u_4_bit_adder_1 (
    .a(a[3:0]), .b(b[3:0]), .carry_in(carry_in), .carry_out(n4_bit_adder_1_carry_out), .\output (out_5[3:0]));
  _4_bit_Adder u_4_bit_adder_2 (
    .a(a[7:4]), .b(b[7:4]), .carry_in(n4_bit_adder_1_carry_out), .carry_out(carry_out), .\output (out_5[7:4]));
endmodule

// 16 A
module _16_bit_Adder (
  input  [15:0] a,
  input  [15:0] b,
  input  carry_in,
  output carry_out,
  output [15:0] \output 
);

  wire n8_bit_adder_1_carry_out;

  _8_bit_Adder u_8_bit_adder_1 (
    .a(a[7:0]), .b(b[7:0]), .carry_in(carry_in), .carry_out(n8_bit_adder_1_carry_out), .out_5(\output [7:0]));
  _8_bit_Adder u_8_bit_adder_2 (
    .a(a[15:8]), .b(b[15:8]), .carry_in(n8_bit_adder_1_carry_out), .carry_out(carry_out),
    .out_5(\output [15:8]));
endmodule

module Incrementer (
  input  [11:0] \input ,
  input  carry_in,
  output carry_out,
  output [11:0] \output 
);

  wire n4_bit_adder_1_carry_out;

  _4_bit_Adder u_4_bit_adder_1 (
    .a(\input [3:0]), .b(4'b0001), .carry_in(carry_in), .carry_out(n4_bit_adder_1_carry_out),
    .\output (\output [3:0]));
  _8_bit_Adder u_8_bit_adder_1 (
    .a(\input [11:4]), .b({8{1'b0}}), .carry_in(n4_bit_adder_1_carry_out), .carry_out(carry_out),
    .out_5(\output [11:4]));
endmodule

// 1 C
module _1_bit_Comparator (
  input  a,
  input  in_gt,
  input  in_eq,
  input  in_lt,
  input  b,
  output out_gt,
  output out_eq,
  output out_lt
);

  wire and_1_out, and_2_out, and_3_out, and_4_out, and_5_out, and_6_out, not_1_out, not_2_out, not_3_out,
       not_4_out, not_5_out, not_6_out, not_7_out, not_8_out, not_9_out, not_10_out, not_11_out, not_12_out,
       not_13_out, not_14_out, not_15_out, not_16_out;

  not not_1 (not_1_out, in_eq);
  not not_2 (not_2_out, in_lt);
  not not_3 (not_3_out, b);
  not not_4 (not_4_out, in_gt);
  not not_5 (not_5_out, in_lt);
  not not_6 (not_6_out, a);
  not not_7 (not_7_out, b);
  not not_8 (not_8_out, in_gt);
  not not_9 (not_9_out, in_lt);
  not not_10 (not_10_out, in_gt);
  not not_11 (not_11_out, in_lt);
  not not_12 (not_12_out, in_gt);
  not not_13 (not_13_out, in_eq);
  not not_14 (not_14_out, a);
  not not_15 (not_15_out, in_gt);
  not not_16 (not_16_out, in_lt);
  and and_1 (and_1_out, in_gt, not_1_out, not_2_out);
  and and_2 (and_2_out, a, not_3_out, not_4_out, in_eq, not_5_out);
  and and_3 (and_3_out, not_6_out, not_7_out, not_8_out, in_eq, not_9_out);
  and and_4 (and_4_out, a, b, not_10_out, in_eq, not_11_out);
  and and_5 (and_5_out, not_12_out, not_13_out, in_lt);
  and and_6 (and_6_out, not_14_out, b, not_15_out, in_eq, not_16_out);
  or or_1 (out_gt, and_1_out, and_2_out);
  or or_2 (out_eq, and_3_out, and_4_out);
  or or_3 (out_lt, and_5_out, and_6_out);
endmodule

// 16 C
module _16_bit_Comparator (
  input  [15:0] input_a,
  input  gt_in,
  input  eq_in,
  input  lt_in,
  input  [15:0] input_b,
  output gt_out,
  output eq_out,
  output lt_out
);

  wire n1_bit_comparator_1_out_eq, n1_bit_comparator_1_out_gt, n1_bit_comparator_1_out_lt,
       n1_bit_comparator_2_out_eq, n1_bit_comparator_2_out_gt, n1_bit_comparator_2_out_lt,
       n1_bit_comparator_3_out_eq, n1_bit_comparator_3_out_gt, n1_bit_comparator_3_out_lt,
       n1_bit_comparator_4_out_eq, n1_bit_comparator_4_out_gt, n1_bit_comparator_4_out_lt,
       n1_bit_comparator_5_out_eq, n1_bit_comparator_5_out_gt, n1_bit_comparator_5_out_lt,
       n1_bit_comparator_6_out_eq, n1_bit_comparator_6_out_gt, n1_bit_comparator_6_out_lt,
       n1_bit_comparator_7_out_eq, n1_bit_comparator_7_out_gt, n1_bit_comparator_7_out_lt,
       n1_bit_comparator_8_out_eq, n1_bit_comparator_8_out_gt, n1_bit_comparator_8_out_lt,
       n1_bit_comparator_9_out_eq, n1_bit_comparator_9_out_gt, n1_bit_comparator_9_out_lt,
       n1_bit_comparator_10_out_eq, n1_bit_comparator_10_out_gt, n1_bit_comparator_10_out_lt,
       n1_bit_comparator_11_out_eq, n1_bit_comparator_11_out_gt, n1_bit_comparator_11_out_lt,
       n1_bit_comparator_12_out_eq, n1_bit_comparator_12_out_gt, n1_bit_comparator_12_out_lt,
       n1_bit_comparator_13_out_eq, n1_bit_comparator_13_out_gt, n1_bit_comparator_13_out_lt,
       n1_bit_comparator_14_out_eq, n1_bit_comparator_14_out_gt, n1_bit_comparator_14_out_lt,
       n1_bit_comparator_15_out_eq, n1_bit_comparator_15_out_gt, n1_bit_comparator_15_out_lt;

  _1_bit_Comparator u_1_bit_comparator_1 (
    .in_gt(n1_bit_comparator_2_out_gt), .in_eq(n1_bit_comparator_2_out_eq),
    .in_lt(n1_bit_comparator_2_out_lt), .a(input_a[14]), .b(input_b[14]),
    .out_gt(n1_bit_comparator_1_out_gt), .out_eq(n1_bit_comparator_1_out_eq),
    .out_lt(n1_bit_comparator_1_out_lt));
  _1_bit_Comparator u_1_bit_comparator_2 (
    .in_gt(gt_in), .in_eq(eq_in), .in_lt(lt_in), .a(input_a[15]), .b(input_b[15]),
    .out_gt(n1_bit_comparator_2_out_gt), .out_eq(n1_bit_comparator_2_out_eq),
    .out_lt(n1_bit_comparator_2_out_lt));
  _1_bit_Comparator u_1_bit_comparator_3 (
    .in_gt(n1_bit_comparator_4_out_gt), .in_eq(n1_bit_comparator_4_out_eq),
    .in_lt(n1_bit_comparator_4_out_lt), .a(input_a[12]), .b(input_b[12]),
    .out_gt(n1_bit_comparator_3_out_gt), .out_eq(n1_bit_comparator_3_out_eq),
    .out_lt(n1_bit_comparator_3_out_lt));
  _1_bit_Comparator u_1_bit_comparator_4 (
    .in_gt(n1_bit_comparator_1_out_gt), .in_eq(n1_bit_comparator_1_out_eq),
    .in_lt(n1_bit_comparator_1_out_lt), .a(input_a[13]), .b(input_b[13]),
    .out_gt(n1_bit_comparator_4_out_gt), .out_eq(n1_bit_comparator_4_out_eq),
    .out_lt(n1_bit_comparator_4_out_lt));
  _1_bit_Comparator u_1_bit_comparator_5 (
    .in_gt(n1_bit_comparator_3_out_gt), .in_eq(n1_bit_comparator_3_out_eq),
    .in_lt(n1_bit_comparator_3_out_lt), .a(input_a[11]), .b(input_b[11]),
    .out_gt(n1_bit_comparator_5_out_gt), .out_eq(n1_bit_comparator_5_out_eq),
    .out_lt(n1_bit_comparator_5_out_lt));
  _1_bit_Comparator u_1_bit_comparator_6 (
    .in_gt(n1_bit_comparator_5_out_gt), .in_eq(n1_bit_comparator_5_out_eq),
    .in_lt(n1_bit_comparator_5_out_lt), .a(input_a[10]), .b(input_b[10]),
    .out_gt(n1_bit_comparator_6_out_gt), .out_eq(n1_bit_comparator_6_out_eq),
    .out_lt(n1_bit_comparator_6_out_lt));
  _1_bit_Comparator u_1_bit_comparator_7 (
    .in_gt(n1_bit_comparator_6_out_gt), .in_eq(n1_bit_comparator_6_out_eq),
    .in_lt(n1_bit_comparator_6_out_lt), .a(input_a[9]), .b(input_b[9]), .out_gt(n1_bit_comparator_7_out_gt),
    .out_eq(n1_bit_comparator_7_out_eq), .out_lt(n1_bit_comparator_7_out_lt));
  _1_bit_Comparator u_1_bit_comparator_8 (
    .in_gt(n1_bit_comparator_7_out_gt), .in_eq(n1_bit_comparator_7_out_eq),
    .in_lt(n1_bit_comparator_7_out_lt), .a(input_a[8]), .b(input_b[8]), .out_gt(n1_bit_comparator_8_out_gt),
    .out_eq(n1_bit_comparator_8_out_eq), .out_lt(n1_bit_comparator_8_out_lt));
  _1_bit_Comparator u_1_bit_comparator_9 (
    .in_gt(n1_bit_comparator_8_out_gt), .in_eq(n1_bit_comparator_8_out_eq),
    .in_lt(n1_bit_comparator_8_out_lt), .a(input_a[7]), .b(input_b[7]), .out_gt(n1_bit_comparator_9_out_gt),
    .out_eq(n1_bit_comparator_9_out_eq), .out_lt(n1_bit_comparator_9_out_lt));
  _1_bit_Comparator u_1_bit_comparator_10 (
    .in_gt(n1_bit_comparator_9_out_gt), .in_eq(n1_bit_comparator_9_out_eq),
    .in_lt(n1_bit_comparator_9_out_lt), .a(input_a[6]), .b(input_b[6]), .out_gt(n1_bit_comparator_10_out_gt),
    .out_eq(n1_bit_comparator_10_out_eq), .out_lt(n1_bit_comparator_10_out_lt));
  _1_bit_Comparator u_1_bit_comparator_11 (
    .in_gt(n1_bit_comparator_10_out_gt), .in_eq(n1_bit_comparator_10_out_eq),
    .in_lt(n1_bit_comparator_10_out_lt), .a(input_a[5]), .b(input_b[5]),
    .out_gt(n1_bit_comparator_11_out_gt), .out_eq(n1_bit_comparator_11_out_eq),
    .out_lt(n1_bit_comparator_11_out_lt));
  _1_bit_Comparator u_1_bit_comparator_12 (
    .in_gt(n1_bit_comparator_11_out_gt), .in_eq(n1_bit_comparator_11_out_eq),
    .in_lt(n1_bit_comparator_11_out_lt), .a(input_a[4]), .b(input_b[4]),
    .out_gt(n1_bit_comparator_12_out_gt), .out_eq(n1_bit_comparator_12_out_eq),
    .out_lt(n1_bit_comparator_12_out_lt));
  _1_bit_Comparator u_1_bit_comparator_13 (
    .in_gt(n1_bit_comparator_14_out_gt), .in_eq(n1_bit_comparator_14_out_eq),
    .in_lt(n1_bit_comparator_14_out_lt), .a(input_a[2]), .b(input_b[2]),
    .out_gt(n1_bit_comparator_13_out_gt), .out_eq(n1_bit_comparator_13_out_eq),
    .out_lt(n1_bit_comparator_13_out_lt));
  _1_bit_Comparator u_1_bit_comparator_14 (
    .in_gt(n1_bit_comparator_12_out_gt), .in_eq(n1_bit_comparator_12_out_eq),
    .in_lt(n1_bit_comparator_12_out_lt), .a(input_a[3]), .b(input_b[3]),
    .out_gt(n1_bit_comparator_14_out_gt), .out_eq(n1_bit_comparator_14_out_eq),
    .out_lt(n1_bit_comparator_14_out_lt));
  _1_bit_Comparator u_1_bit_comparator_15 (
    .in_gt(n1_bit_comparator_13_out_gt), .in_eq(n1_bit_comparator_13_out_eq),
    .in_lt(n1_bit_comparator_13_out_lt), .a(input_a[1]), .b(input_b[1]),
    .out_gt(n1_bit_comparator_15_out_gt), .out_eq(n1_bit_comparator_15_out_eq),
    .out_lt(n1_bit_comparator_15_out_lt));
  _1_bit_Comparator u_1_bit_comparator_16 (
    .in_gt(n1_bit_comparator_15_out_gt), .in_eq(n1_bit_comparator_15_out_eq),
    .in_lt(n1_bit_comparator_15_out_lt), .a(input_a[0]), .b(input_b[0]), .out_gt(gt_out), .out_eq(eq_out),
    .out_lt(lt_out));
endmodule

module ALU (
  input  [15:0] input_a,
  input  [15:0] input_b,
  input  ALUcontrol,
  output [15:0] out_4
);

  wire [15:0] and_1_out, n16_bit_adder_1_output;

  assign and_1_out = input_b & input_a;  // AND_Gate and_1, 16 bits wide
  _16_bit_Adder u_16_bit_adder_1 (
    .a(input_a), .b(input_b), .carry_in(1'b0), .\output (n16_bit_adder_1_output));  // open: carry_out
  Multiplexer #(.width(16)) multiplexer_1 (
    .in0(and_1_out), .in1(n16_bit_adder_1_output), .out(out_4), .sel(ALUcontrol));  // open: en
endmodule

module Control_Unit (
  input  [15:0] instruction,
  output dataMemRead,
  output dataMemWrite,
  output regRead,
  output regWrite,
  output ALUand,
  output ALUadd,
  output comparator,
  output PCselect
);

  wire decoder_1_out0, decoder_1_out1, decoder_1_out2, decoder_1_out3, decoder_1_out7, decoder_1_out8,
       decoder_1_out9, decoder_1_out10, decoder_1_out11, decoder_1_out12;

  Decoder #(.select(4)) decoder_1 (
    .out0(decoder_1_out0), .out1(decoder_1_out1), .out2(decoder_1_out2), .out3(decoder_1_out3),
    .out4(dataMemRead), .out5(dataMemWrite), .out6(comparator), .out7(decoder_1_out7), .out8(decoder_1_out8),
    .out9(decoder_1_out9), .out10(decoder_1_out10), .out11(decoder_1_out11), .out12(decoder_1_out12),
    .sel(instruction[3:0]));  // open: out13, out14, out15, en
  or u_regRead (regRead, decoder_1_out0, decoder_1_out1, decoder_1_out2, decoder_1_out3, dataMemWrite);
  or u_regWrite (regWrite, decoder_1_out0, decoder_1_out1, decoder_1_out2, decoder_1_out3, dataMemRead);
  or u_ALUand (ALUand, decoder_1_out2, decoder_1_out3);
  or u_ALUadd (ALUadd, decoder_1_out0, decoder_1_out1, decoder_1_out7);
  or u_PCselect (PCselect, decoder_1_out7, decoder_1_out8, decoder_1_out9, decoder_1_out10, decoder_1_out11, decoder_1_out12);
endmodule
